# Fritzing sketch servo_sketch (saved by Fritzing 0.9.3b)
breadboards: 1

parts:
  Part1 = Arduino Nano (Rev3.0)
  J1 = Basic Servo
  J2 = Basic Servo

nets:
  GND: Part1.GND, J1.gnd, J2.gnd
  N1: Part1.D11/MOSI, J1.pulse
  N2: Part1.D12/MISO, J2.pulse
  VCC: Part1.5V, J1.vcc, J2.vcc
